# Fritzing sketch Esquema Conexion HM10 (saved by Fritzing 0.9.10b)
breadboards: 1

parts:
  Componente1 = Bluetooth HM-10
  WeMos_D1_Mini1 = WeMos D1 Mini

nets:
  N1: Componente1.RXD, WeMos_D1_Mini1.D6
  N2: Componente1.TXD, WeMos_D1_Mini1.D5
  N3: Componente1.GND, WeMos_D1_Mini1.G
  VCC: Componente1.VCC, WeMos_D1_Mini1.3V3
