# Fritzing sketch Conexion GPS (saved by Fritzing 0.9.10b)
breadboards: 1

parts:
  M1 = NEO-6M GPS Module [part_number=GY-GPS6MV2]
  WeMos_D1_Mini1 = WeMos D1 Mini

nets:
  N1: M1.GND, WeMos_D1_Mini1.G
  N2: M1.Tx, WeMos_D1_Mini1.D2
  N3: M1.Rx, WeMos_D1_Mini1.RX
  VCC: M1.Vcc, WeMos_D1_Mini1.5V

custom parts:
  NEO-6M GPS Module: GY-GPS6MV2 NEO-6M GPS Module Module based on U-blox NEO-6M GPS engine, incorporating regulator for 3.3-5V DC input, MS621FE-compatible rechargeable battery for backup and EEPROM for storing configuration settings. Links: NEO-6 series product information page NEO-6 Datasheet
